// Logisim project LastProject.circ as structural Verilog
module FullAdder (
  input  A,
  input  B,
  input  C___in,
  output Sum,
  output C___out
);

  wire and_1_out, and_2_out, xor_1_out;

  xor xor_1 (xor_1_out, A, B);
  xor xor_2 (Sum, xor_1_out, C___in);
  and and_1 (and_1_out, C___in, xor_1_out);
  and and_2 (and_2_out, B, A);
  or or_1 (C___out, and_1_out, and_2_out);
endmodule

module HalfCompare (
  input  A,
  input  B,
  output LT,
  output GT,
  output EQ
);

  wire not_1_out, not_2_out;

  not not_1 (not_1_out, A);
  not not_2 (not_2_out, B);
  and and_1 (LT, not_1_out, B);
  and and_2 (GT, A, not_2_out);
  xnor xnor_1 (EQ, A, B);
endmodule

module HalfAdder (
  input  A,
  input  B,
  output S,
  output C
);

  xor xor_1 (S, A, B);
  and and_1 (C, A, B);
endmodule

module HalfSubtractor (
  input  A,
  input  B,
  output Difference,
  output Barrow
);

  wire not_1_out;

  not not_1 (not_1_out, A);
  and and_1 (Barrow, not_1_out, B);
  xor xor_1 (Difference, A, B);
endmodule

module FullCompare (
  input  A,
  input  B,
  input  LT___Inp,
  input  GT___Inp,
  input  EQ___Inp,
  output LESS_THAN,
  output GREATER_THAN,
  output EQUAL
);

  wire and_1_out, and_2_out, not_1_out, not_2_out, not_3_out, not_4_out, or_1_out, or_2_out, xnor_1_out;

  not not_1 (not_1_out, A);
  and and_1 (and_1_out, not_1_out, B);
  and and_2 (and_2_out, A, not_2_out);
  not not_2 (not_2_out, B);
  xnor xnor_1 (xnor_1_out, B, A);
  not not_3 (not_3_out, GT___Inp);
  or or_1 (or_1_out, and_1_out, LT___Inp);
  or or_2 (or_2_out, GT___Inp, and_2_out);
  not not_4 (not_4_out, LT___Inp);
  and and_3 (EQUAL, EQ___Inp, xnor_1_out);
  and and_4 (LESS_THAN, not_3_out, or_1_out);
  and and_5 (GREATER_THAN, or_2_out, not_4_out);
endmodule

module DLatch (
  input  D,
  input  CLK,
  output out_3
);

  wire and_1_out, and_2_out, nor_1_out, not_1_out;

  and and_1 (and_1_out, D, CLK);
  and and_2 (and_2_out, CLK, not_1_out);
  not not_1 (not_1_out, D);
  nor nor_1 (nor_1_out, and_1_out, out_3);
  nor nor_2 (out_3, and_2_out, nor_1_out);
endmodule

module _20BitFlipFlop (
  input  [19:0] in_1,
  output [19:0] out_2
);

  wire clock_1_out;

  Clock clock_1 (.out(clock_1_out));
  DLatch dlatch_1 (.D(in_1[19]), .CLK(clock_1_out), .out_3(out_2[19]));
  DLatch dlatch_2 (.D(in_1[18]), .CLK(clock_1_out), .out_3(out_2[18]));
  DLatch dlatch_3 (.D(in_1[17]), .CLK(clock_1_out), .out_3(out_2[17]));
  DLatch dlatch_4 (.D(in_1[16]), .CLK(clock_1_out), .out_3(out_2[16]));
  DLatch dlatch_5 (.D(in_1[15]), .CLK(clock_1_out), .out_3(out_2[15]));
  DLatch dlatch_6 (.D(in_1[14]), .CLK(clock_1_out), .out_3(out_2[14]));
  DLatch dlatch_7 (.D(in_1[13]), .CLK(clock_1_out), .out_3(out_2[13]));
  DLatch dlatch_8 (.D(in_1[12]), .CLK(clock_1_out), .out_3(out_2[12]));
  DLatch dlatch_9 (.D(in_1[11]), .CLK(clock_1_out), .out_3(out_2[11]));
  DLatch dlatch_10 (.D(in_1[10]), .CLK(clock_1_out), .out_3(out_2[10]));
  DLatch dlatch_11 (.D(in_1[9]), .CLK(clock_1_out), .out_3(out_2[9]));
  DLatch dlatch_12 (.D(in_1[8]), .CLK(clock_1_out), .out_3(out_2[8]));
  DLatch dlatch_13 (.D(in_1[7]), .CLK(clock_1_out), .out_3(out_2[7]));
  DLatch dlatch_14 (.D(in_1[6]), .CLK(clock_1_out), .out_3(out_2[6]));
  DLatch dlatch_15 (.D(in_1[5]), .CLK(clock_1_out), .out_3(out_2[5]));
  DLatch dlatch_16 (.D(in_1[4]), .CLK(clock_1_out), .out_3(out_2[4]));
  DLatch dlatch_17 (.D(in_1[3]), .CLK(clock_1_out), .out_3(out_2[3]));
  DLatch dlatch_18 (.D(in_1[2]), .CLK(clock_1_out), .out_3(out_2[2]));
  DLatch dlatch_19 (.D(in_1[1]), .CLK(clock_1_out), .out_3(out_2[1]));
  DLatch dlatch_20 (.D(in_1[0]), .CLK(clock_1_out), .out_3(out_2[0]));
endmodule

module Adder (
  input  [19:0] A,
  input  [19:0] B,
  output [19:0] Output
);

  wire fulladder_2_c___out, fulladder_3_c___out, fulladder_4_c___out, fulladder_5_c___out,
       fulladder_6_c___out, fulladder_7_c___out, fulladder_8_c___out, fulladder_9_c___out,
       fulladder_10_c___out, fulladder_11_c___out, fulladder_12_c___out, fulladder_13_c___out,
       fulladder_14_c___out, fulladder_15_c___out, fulladder_16_c___out, fulladder_17_c___out,
       fulladder_18_c___out, fulladder_19_c___out, halfadder_1_c;

  FullAdder fulladder_1 (.A(B[19]), .B(A[19]), .C___in(fulladder_2_c___out), .Sum(Output[19]));  // open: C___out
  FullAdder fulladder_2 (
    .A(B[18]), .B(A[18]), .C___in(fulladder_4_c___out), .Sum(Output[18]), .C___out(fulladder_2_c___out));
  FullAdder fulladder_3 (
    .A(B[16]), .B(A[16]), .C___in(fulladder_5_c___out), .Sum(Output[16]), .C___out(fulladder_3_c___out));
  FullAdder fulladder_4 (
    .A(B[17]), .B(A[17]), .C___in(fulladder_3_c___out), .Sum(Output[17]), .C___out(fulladder_4_c___out));
  FullAdder fulladder_5 (
    .A(B[15]), .B(A[15]), .C___in(fulladder_6_c___out), .Sum(Output[15]), .C___out(fulladder_5_c___out));
  FullAdder fulladder_6 (
    .A(B[14]), .B(A[14]), .C___in(fulladder_8_c___out), .Sum(Output[14]), .C___out(fulladder_6_c___out));
  FullAdder fulladder_7 (
    .A(B[12]), .B(A[12]), .C___in(fulladder_9_c___out), .Sum(Output[12]), .C___out(fulladder_7_c___out));
  FullAdder fulladder_8 (
    .A(B[13]), .B(A[13]), .C___in(fulladder_7_c___out), .Sum(Output[13]), .C___out(fulladder_8_c___out));
  FullAdder fulladder_9 (
    .A(B[11]), .B(A[11]), .C___in(fulladder_10_c___out), .Sum(Output[11]), .C___out(fulladder_9_c___out));
  FullAdder fulladder_10 (
    .A(B[10]), .B(A[10]), .C___in(fulladder_12_c___out), .Sum(Output[10]), .C___out(fulladder_10_c___out));
  FullAdder fulladder_11 (
    .A(B[8]), .B(A[8]), .C___in(fulladder_13_c___out), .Sum(Output[8]), .C___out(fulladder_11_c___out));
  FullAdder fulladder_12 (
    .A(B[9]), .B(A[9]), .C___in(fulladder_11_c___out), .Sum(Output[9]), .C___out(fulladder_12_c___out));
  FullAdder fulladder_13 (
    .A(B[7]), .B(A[7]), .C___in(fulladder_14_c___out), .Sum(Output[7]), .C___out(fulladder_13_c___out));
  FullAdder fulladder_14 (
    .A(B[6]), .B(A[6]), .C___in(fulladder_16_c___out), .Sum(Output[6]), .C___out(fulladder_14_c___out));
  FullAdder fulladder_15 (
    .A(B[4]), .B(A[4]), .C___in(fulladder_17_c___out), .Sum(Output[4]), .C___out(fulladder_15_c___out));
  FullAdder fulladder_16 (
    .A(B[5]), .B(A[5]), .C___in(fulladder_15_c___out), .Sum(Output[5]), .C___out(fulladder_16_c___out));
  FullAdder fulladder_17 (
    .A(B[3]), .B(A[3]), .C___in(fulladder_18_c___out), .Sum(Output[3]), .C___out(fulladder_17_c___out));
  FullAdder fulladder_18 (
    .A(B[2]), .B(A[2]), .C___in(fulladder_19_c___out), .Sum(Output[2]), .C___out(fulladder_18_c___out));
  HalfAdder halfadder_1 (.A(B[0]), .B(A[0]), .S(Output[0]), .C(halfadder_1_c));
  FullAdder fulladder_19 (.A(B[1]), .B(A[1]), .C___in(halfadder_1_c), .Sum(Output[1]), .C___out(fulladder_19_c___out));
endmodule

module Subtractor (
  input  [19:0] A,
  input  [19:0] B,
  output [19:0] out_3
);

  wire [19:0] adder_2_output, B_out;

  assign B_out = ~B;  // NOT_Gate B, 20 bits wide
  Adder adder_1 (.A(A), .B(adder_2_output), .Output(out_3));
  Adder adder_2 (.A(B_out), .B(20'h1), .Output(adder_2_output));
endmodule

module FlipFlop (
  input  D,
  input  CLK,
  output out_3
);

  wire dlatch_1_out_3, not_1_out;

  not not_1 (not_1_out, CLK);
  DLatch dlatch_1 (.D(D), .CLK(not_1_out), .out_3(dlatch_1_out_3));
  DLatch dlatch_2 (.D(dlatch_1_out_3), .CLK(CLK), .out_3(out_3));
endmodule

module ShiftLeftOneBit (
  input  D0,
  input  [19:0] Number,
  output [19:0] D1
);

  wire [19:0] and_1_out, and_2_out, not_1_out;

  assign not_1_out = ~{20{D0}};  // NOT_Gate not_1, 20 bits wide
  assign and_1_out = not_1_out & Number;  // AND_Gate and_1, 20 bits wide
  assign and_2_out = Number & {20{D0}};  // AND_Gate and_2, 20 bits wide
  assign D1 = and_1_out | {and_2_out[18:0], 1'b0};  // OR_Gate or_1, 20 bits wide
endmodule

// D2
module ShiftLeftTwoBit (
  input  D1,
  input  [19:0] Number,
  output [19:0] out_3
);

  wire [19:0] and_1_out, and_2_out, not_1_out;

  assign not_1_out = ~{20{D1}};  // NOT_Gate not_1, 20 bits wide
  assign and_1_out = not_1_out & Number;  // AND_Gate and_1, 20 bits wide
  assign and_2_out = Number & {20{D1}};  // AND_Gate and_2, 20 bits wide
  assign out_3 = and_1_out | {and_2_out[17:0], 2'b00};  // OR_Gate or_1, 20 bits wide
endmodule

// D3
module ShiftLeftFourBit (
  input  D2,
  input  [19:0] Number,
  output [19:0] out_3
);

  wire [19:0] and_1_out, and_2_out, not_1_out;

  assign not_1_out = ~{20{D2}};  // NOT_Gate not_1, 20 bits wide
  assign and_1_out = not_1_out & Number;  // AND_Gate and_1, 20 bits wide
  assign and_2_out = Number & {20{D2}};  // AND_Gate and_2, 20 bits wide
  assign out_3 = and_1_out | {and_2_out[15:0], 4'b0000};  // OR_Gate or_1, 20 bits wide
endmodule

// D4
module ShiftLeftEightBit (
  input  D3,
  input  [19:0] Number,
  output [19:0] out_3
);

  wire [19:0] and_1_out, and_2_out, not_1_out;

  assign not_1_out = ~{20{D3}};  // NOT_Gate not_1, 20 bits wide
  assign and_1_out = not_1_out & Number;  // AND_Gate and_1, 20 bits wide
  assign and_2_out = Number & {20{D3}};  // AND_Gate and_2, 20 bits wide
  assign out_3 = and_1_out | {and_2_out[11:0], {8{1'b0}}};  // OR_Gate or_1, 20 bits wide
endmodule

// 21
module ShiftLeftSixteenBit (
  input  D4,
  input  [19:0] Number,
  output [19:0] Result
);

  wire [19:0] and_1_out, and_2_out, not_1_out;

  assign not_1_out = ~{20{D4}};  // NOT_Gate not_1, 20 bits wide
  assign and_1_out = not_1_out & Number;  // AND_Gate and_1, 20 bits wide
  assign and_2_out = Number & {20{D4}};  // AND_Gate and_2, 20 bits wide
  assign Result = and_1_out | {and_2_out[3:0], {16{1'b0}}};  // OR_Gate or_1, 20 bits wide
endmodule

module LeftShifter (
  input  [19:0] Input,
  input  [19:0] Shift,
  output [19:0] Output
);

  wire [19:0] shiftlefteightbit_1_out_3, shiftleftfourbit_1_out_3, shiftleftonebit_1_d1,
       shiftleftsixteenbit_1_result, shiftlefttwobit_1_out_3;
  wire [19:19] nor_1_out;

  nor nor_1 (nor_1_out[19], Shift[5], Shift[6], Shift[7], Shift[8], Shift[9], Shift[10], Shift[11], Shift[12], Shift[13], Shift[14], Shift[15], Shift[16], Shift[17], Shift[18], Shift[19]);
  ShiftLeftOneBit shiftleftonebit_1 (.D0(Shift[0]), .Number(Input), .D1(shiftleftonebit_1_d1));
  ShiftLeftTwoBit shiftlefttwobit_1 (.D1(Shift[1]), .Number(shiftleftonebit_1_d1), .out_3(shiftlefttwobit_1_out_3));
  ShiftLeftFourBit shiftleftfourbit_1 (
    .D2(Shift[2]), .Number(shiftlefttwobit_1_out_3), .out_3(shiftleftfourbit_1_out_3));
  ShiftLeftEightBit shiftlefteightbit_1 (
    .D3(Shift[3]), .Number(shiftleftfourbit_1_out_3), .out_3(shiftlefteightbit_1_out_3));
  ShiftLeftSixteenBit shiftleftsixteenbit_1 (
    .D4(Shift[4]), .Number(shiftlefteightbit_1_out_3), .Result(shiftleftsixteenbit_1_result));
  assign Output = {20{nor_1_out[19]}} & shiftleftsixteenbit_1_result;  // AND_Gate and_1, 20 bits wide
endmodule

module Register (
  input  [19:0] D,
  input  Load_EN,
  input  CLK,
  input  clear,
  output [19:0] out_5
);

  wire [19:0] flipflop_19_out_3, multiplexer_1_out;

  Multiplexer #(.width(20), .enable("false")) multiplexer_1 (
    .in0(out_5), .in1(D), .out(multiplexer_1_out), .sel(Load_EN));
  FlipFlop flipflop_1 (.D(multiplexer_1_out[19]), .CLK(CLK), .out_3(flipflop_19_out_3[19]));
  FlipFlop flipflop_2 (.D(multiplexer_1_out[18]), .CLK(CLK), .out_3(flipflop_19_out_3[18]));
  FlipFlop flipflop_3 (.D(multiplexer_1_out[17]), .CLK(CLK), .out_3(flipflop_19_out_3[17]));
  FlipFlop flipflop_4 (.D(multiplexer_1_out[16]), .CLK(CLK), .out_3(flipflop_19_out_3[16]));
  FlipFlop flipflop_5 (.D(multiplexer_1_out[15]), .CLK(CLK), .out_3(flipflop_19_out_3[15]));
  FlipFlop flipflop_6 (.D(multiplexer_1_out[14]), .CLK(CLK), .out_3(flipflop_19_out_3[14]));
  FlipFlop flipflop_7 (.D(multiplexer_1_out[12]), .CLK(CLK), .out_3(flipflop_19_out_3[12]));
  FlipFlop flipflop_8 (.D(multiplexer_1_out[13]), .CLK(CLK), .out_3(flipflop_19_out_3[13]));
  FlipFlop flipflop_9 (.D(multiplexer_1_out[11]), .CLK(CLK), .out_3(flipflop_19_out_3[11]));
  FlipFlop flipflop_10 (.D(multiplexer_1_out[10]), .CLK(CLK), .out_3(flipflop_19_out_3[10]));
  FlipFlop flipflop_11 (.D(multiplexer_1_out[9]), .CLK(CLK), .out_3(flipflop_19_out_3[9]));
  FlipFlop flipflop_12 (.D(multiplexer_1_out[8]), .CLK(CLK), .out_3(flipflop_19_out_3[8]));
  FlipFlop flipflop_13 (.D(multiplexer_1_out[7]), .CLK(CLK), .out_3(flipflop_19_out_3[7]));
  FlipFlop flipflop_14 (.D(multiplexer_1_out[6]), .CLK(CLK), .out_3(flipflop_19_out_3[6]));
  FlipFlop flipflop_15 (.D(multiplexer_1_out[4]), .CLK(CLK), .out_3(flipflop_19_out_3[4]));
  FlipFlop flipflop_16 (.D(multiplexer_1_out[5]), .CLK(CLK), .out_3(flipflop_19_out_3[5]));
  FlipFlop flipflop_17 (.D(multiplexer_1_out[3]), .CLK(CLK), .out_3(flipflop_19_out_3[3]));
  FlipFlop flipflop_18 (.D(multiplexer_1_out[2]), .CLK(CLK), .out_3(flipflop_19_out_3[2]));
  FlipFlop flipflop_19 (.D(multiplexer_1_out[0]), .CLK(CLK), .out_3(flipflop_19_out_3[0]));
  FlipFlop flipflop_20 (.D(multiplexer_1_out[1]), .CLK(CLK), .out_3(flipflop_19_out_3[1]));
  Multiplexer #(.width(20), .enable("false")) multiplexer_2 (
    .in0({20{1'b0}}), .in1(flipflop_19_out_3), .out(out_5), .sel(clear));
endmodule

module Compare (
  input  [19:0] A,
  input  [19:0] B,
  input  [2:0] LEG,
  output out_4
);

  wire and_1_out, and_2_out, and_3_out, fullcompare_1_equal, fullcompare_1_greater_than,
       fullcompare_1_less_than, fullcompare_2_equal, fullcompare_2_greater_than, fullcompare_2_less_than,
       fullcompare_3_equal, fullcompare_3_greater_than, fullcompare_3_less_than, fullcompare_4_equal,
       fullcompare_4_greater_than, fullcompare_4_less_than, fullcompare_5_equal, fullcompare_5_greater_than,
       fullcompare_5_less_than, fullcompare_6_equal, fullcompare_6_greater_than, fullcompare_6_less_than,
       fullcompare_7_equal, fullcompare_7_greater_than, fullcompare_7_less_than, fullcompare_8_equal,
       fullcompare_8_greater_than, fullcompare_8_less_than, fullcompare_9_equal, fullcompare_9_greater_than,
       fullcompare_9_less_than, fullcompare_10_equal, fullcompare_10_greater_than, fullcompare_10_less_than,
       fullcompare_11_equal, fullcompare_11_greater_than, fullcompare_11_less_than, fullcompare_12_equal,
       fullcompare_12_greater_than, fullcompare_12_less_than, fullcompare_13_equal,
       fullcompare_13_greater_than, fullcompare_13_less_than, fullcompare_14_equal,
       fullcompare_14_greater_than, fullcompare_14_less_than, fullcompare_15_equal,
       fullcompare_15_greater_than, fullcompare_15_less_than, fullcompare_16_equal,
       fullcompare_16_greater_than, fullcompare_16_less_than, fullcompare_17_equal,
       fullcompare_17_greater_than, fullcompare_17_less_than, fullcompare_18_equal,
       fullcompare_18_greater_than, fullcompare_18_less_than, fullcompare_19_equal,
       fullcompare_19_greater_than, fullcompare_19_less_than, halfcompare_1_eq, halfcompare_1_gt,
       halfcompare_1_lt;

  HalfCompare halfcompare_1 (.A(A[19]), .B(B[19]), .LT(halfcompare_1_lt), .GT(halfcompare_1_gt), .EQ(halfcompare_1_eq));
  FullCompare fullcompare_1 (
    .A(A[17]), .B(B[17]), .LT___Inp(fullcompare_2_less_than), .GT___Inp(fullcompare_2_greater_than),
    .EQ___Inp(fullcompare_2_equal), .LESS_THAN(fullcompare_1_less_than),
    .GREATER_THAN(fullcompare_1_greater_than), .EQUAL(fullcompare_1_equal));
  FullCompare fullcompare_2 (
    .A(A[18]), .B(B[18]), .LT___Inp(halfcompare_1_gt), .GT___Inp(halfcompare_1_lt),
    .EQ___Inp(halfcompare_1_eq), .LESS_THAN(fullcompare_2_less_than),
    .GREATER_THAN(fullcompare_2_greater_than), .EQUAL(fullcompare_2_equal));
  FullCompare fullcompare_3 (
    .A(A[16]), .B(B[16]), .LT___Inp(fullcompare_1_less_than), .GT___Inp(fullcompare_1_greater_than),
    .EQ___Inp(fullcompare_1_equal), .LESS_THAN(fullcompare_3_less_than),
    .GREATER_THAN(fullcompare_3_greater_than), .EQUAL(fullcompare_3_equal));
  FullCompare fullcompare_4 (
    .A(A[15]), .B(B[15]), .LT___Inp(fullcompare_3_less_than), .GT___Inp(fullcompare_3_greater_than),
    .EQ___Inp(fullcompare_3_equal), .LESS_THAN(fullcompare_4_less_than),
    .GREATER_THAN(fullcompare_4_greater_than), .EQUAL(fullcompare_4_equal));
  FullCompare fullcompare_5 (
    .A(A[13]), .B(B[13]), .LT___Inp(fullcompare_6_less_than), .GT___Inp(fullcompare_6_greater_than),
    .EQ___Inp(fullcompare_6_equal), .LESS_THAN(fullcompare_5_less_than),
    .GREATER_THAN(fullcompare_5_greater_than), .EQUAL(fullcompare_5_equal));
  FullCompare fullcompare_6 (
    .A(A[14]), .B(B[14]), .LT___Inp(fullcompare_4_less_than), .GT___Inp(fullcompare_4_greater_than),
    .EQ___Inp(fullcompare_4_equal), .LESS_THAN(fullcompare_6_less_than),
    .GREATER_THAN(fullcompare_6_greater_than), .EQUAL(fullcompare_6_equal));
  FullCompare fullcompare_7 (
    .A(A[12]), .B(B[12]), .LT___Inp(fullcompare_5_less_than), .GT___Inp(fullcompare_5_greater_than),
    .EQ___Inp(fullcompare_5_equal), .LESS_THAN(fullcompare_7_less_than),
    .GREATER_THAN(fullcompare_7_greater_than), .EQUAL(fullcompare_7_equal));
  FullCompare fullcompare_8 (
    .A(A[11]), .B(B[11]), .LT___Inp(fullcompare_7_less_than), .GT___Inp(fullcompare_7_greater_than),
    .EQ___Inp(fullcompare_7_equal), .LESS_THAN(fullcompare_8_less_than),
    .GREATER_THAN(fullcompare_8_greater_than), .EQUAL(fullcompare_8_equal));
  FullCompare fullcompare_9 (
    .A(A[9]), .B(B[9]), .LT___Inp(fullcompare_10_less_than), .GT___Inp(fullcompare_10_greater_than),
    .EQ___Inp(fullcompare_10_equal), .LESS_THAN(fullcompare_9_less_than),
    .GREATER_THAN(fullcompare_9_greater_than), .EQUAL(fullcompare_9_equal));
  FullCompare fullcompare_10 (
    .A(A[10]), .B(B[10]), .LT___Inp(fullcompare_8_less_than), .GT___Inp(fullcompare_8_greater_than),
    .EQ___Inp(fullcompare_8_equal), .LESS_THAN(fullcompare_10_less_than),
    .GREATER_THAN(fullcompare_10_greater_than), .EQUAL(fullcompare_10_equal));
  FullCompare fullcompare_11 (
    .A(A[8]), .B(B[8]), .LT___Inp(fullcompare_9_less_than), .GT___Inp(fullcompare_9_greater_than),
    .EQ___Inp(fullcompare_9_equal), .LESS_THAN(fullcompare_11_less_than),
    .GREATER_THAN(fullcompare_11_greater_than), .EQUAL(fullcompare_11_equal));
  FullCompare fullcompare_12 (
    .A(A[7]), .B(B[7]), .LT___Inp(fullcompare_11_less_than), .GT___Inp(fullcompare_11_greater_than),
    .EQ___Inp(fullcompare_11_equal), .LESS_THAN(fullcompare_12_less_than),
    .GREATER_THAN(fullcompare_12_greater_than), .EQUAL(fullcompare_12_equal));
  FullCompare fullcompare_13 (
    .A(A[5]), .B(B[5]), .LT___Inp(fullcompare_14_less_than), .GT___Inp(fullcompare_14_greater_than),
    .EQ___Inp(fullcompare_14_equal), .LESS_THAN(fullcompare_13_less_than),
    .GREATER_THAN(fullcompare_13_greater_than), .EQUAL(fullcompare_13_equal));
  FullCompare fullcompare_14 (
    .A(A[6]), .B(B[6]), .LT___Inp(fullcompare_12_less_than), .GT___Inp(fullcompare_12_greater_than),
    .EQ___Inp(fullcompare_12_equal), .LESS_THAN(fullcompare_14_less_than),
    .GREATER_THAN(fullcompare_14_greater_than), .EQUAL(fullcompare_14_equal));
  FullCompare fullcompare_15 (
    .A(A[4]), .B(B[4]), .LT___Inp(fullcompare_13_less_than), .GT___Inp(fullcompare_13_greater_than),
    .EQ___Inp(fullcompare_13_equal), .LESS_THAN(fullcompare_15_less_than),
    .GREATER_THAN(fullcompare_15_greater_than), .EQUAL(fullcompare_15_equal));
  FullCompare fullcompare_16 (
    .A(A[3]), .B(B[3]), .LT___Inp(fullcompare_15_less_than), .GT___Inp(fullcompare_15_greater_than),
    .EQ___Inp(fullcompare_15_equal), .LESS_THAN(fullcompare_16_less_than),
    .GREATER_THAN(fullcompare_16_greater_than), .EQUAL(fullcompare_16_equal));
  FullCompare fullcompare_17 (
    .A(A[1]), .B(B[1]), .LT___Inp(fullcompare_18_less_than), .GT___Inp(fullcompare_18_greater_than),
    .EQ___Inp(fullcompare_18_equal), .LESS_THAN(fullcompare_17_less_than),
    .GREATER_THAN(fullcompare_17_greater_than), .EQUAL(fullcompare_17_equal));
  FullCompare fullcompare_18 (
    .A(A[2]), .B(B[2]), .LT___Inp(fullcompare_16_less_than), .GT___Inp(fullcompare_16_greater_than),
    .EQ___Inp(fullcompare_16_equal), .LESS_THAN(fullcompare_18_less_than),
    .GREATER_THAN(fullcompare_18_greater_than), .EQUAL(fullcompare_18_equal));
  FullCompare fullcompare_19 (
    .A(A[0]), .B(B[0]), .LT___Inp(fullcompare_17_less_than), .GT___Inp(fullcompare_17_greater_than),
    .EQ___Inp(fullcompare_17_equal), .LESS_THAN(fullcompare_19_less_than),
    .GREATER_THAN(fullcompare_19_greater_than), .EQUAL(fullcompare_19_equal));
  and and_1 (and_1_out, fullcompare_19_less_than, LEG[2]);
  and and_2 (and_2_out, fullcompare_19_greater_than, LEG[0]);
  and and_3 (and_3_out, fullcompare_19_equal, LEG[1]);
  or or_1 (out_4, and_1_out, and_2_out, and_3_out);
endmodule

module ALU (
  input  [19:0] A,
  input  [19:0] B,
  input  [2:0] ALU_Bits,
  output [19:0] out_4
);

  wire [19:0] adder_1_output, leftshifter_1_output, nand_1_out, or_1_out, subtractor_1_out_3;

  LeftShifter leftshifter_1 (.Input(A), .Shift(B), .Output(leftshifter_1_output));
  Adder adder_1 (.A(A), .B(B), .Output(adder_1_output));
  Subtractor subtractor_1 (.A(A), .B(B), .out_3(subtractor_1_out_3));
  assign or_1_out = A | B;  // OR_Gate or_1, 20 bits wide
  assign nand_1_out = ~(A & B);  // NAND_Gate nand_1, 20 bits wide
  Multiplexer #(.select(3), .width(20), .enable("false")) multiplexer_1 (
    .in0(adder_1_output), .in1(subtractor_1_out_3), .in2(or_1_out), .in3(nand_1_out),
    .in4(leftshifter_1_output), .in5(leftshifter_1_output), .in6(leftshifter_1_output),
    .in7(leftshifter_1_output), .out(out_4), .sel(ALU_Bits));
endmodule

module try (
  input  in_1,
  output [19:0] out_2,
  output [19:0] out_3
);

  wire checkloadstorebranch_1_load, checkloadstorebranch_1_loadenable, checkloadstorebranch_1_store, Clock,
       not_1_out, registernum_1_isimmediate;
  wire [3:0] registernum_1_destreg, registernum_1_sourcer1, registernum_1_sourcer2;
  wire [11:0] shrink20to12_1__12bit;
  wire [19:0] A, B, instruction, multiplexer_2_out, ram_1_data, register_1_out_5, registerflie_1_read_2,
       registernum_1_immediate, rom_1_data;

  Clock clock_1 (.out(Clock));
  Multiplexer #(.width(20), .enable("false")) multiplexer_1 (
    .in0({20{1'b0}}), .in1(rom_1_data), .out(instruction), .sel(in_1));
  Shrink20to12 shrink20to12_1 (._20Bit(register_1_out_5), ._12Bit(shrink20to12_1__12bit));
  CheckLoadStoreBranch checkloadstorebranch_1 (
    .instruction(instruction), .LoadEnable(checkloadstorebranch_1_loadenable),
    .Load(checkloadstorebranch_1_load), .Store(checkloadstorebranch_1_store));
  ALU alu_1 (.A(A), .B(B), .ALU_Bits(instruction[18:16]), .out_4(out_2));
  ROM #(.addrWidth(12), .dataWidth(20)) rom_1 (.addr(shrink20to12_1__12bit), .data(rom_1_data), .sel(in_1));
  Multiplexer #(.width(20), .enable("false")) multiplexer_2 (
    .in0(out_2), .in1(ram_1_data), .out(multiplexer_2_out), .sel(checkloadstorebranch_1_load));
  RegisterNum registernum_1 (
    .instruction(instruction), .SourceR2(registernum_1_sourcer2), .SourceR1(registernum_1_sourcer1),
    .DestReg(registernum_1_destreg), .Immediate(registernum_1_immediate),
    .IsImmediate(registernum_1_isimmediate));
  RegisterFlie registerflie_1 (
    .D(multiplexer_2_out), .load_EN(checkloadstorebranch_1_loadenable), .\reg (registernum_1_destreg),
    .CLK(Clock), .start(in_1), .Read_reg1(registernum_1_sourcer1), .Read_reg2(registernum_1_sourcer2),
    .Read_1(A), .Read_2(registerflie_1_read_2));
  Multiplexer #(.width(20), .enable("false")) multiplexer_3 (
    .in0(registerflie_1_read_2), .in1(registernum_1_immediate), .out(B), .sel(registernum_1_isimmediate));
  Register register_1 (.D(out_3), .CLK(Clock), .Load_EN(in_1), .clear(in_1), .out_5(register_1_out_5));
  RAM #(.addrWidth(20), .dataWidth(20), .bus("separate")) ram_1 (
    .addr(B), .din(A), .data(ram_1_data), .str(checkloadstorebranch_1_store), .sel(1'b1), .clk(Clock),
    .ld(checkloadstorebranch_1_load), .clr(not_1_out));
  not not_1 (not_1_out, in_1);
  Compare_JUMP compare_jump_1 (
    .A(A), .B(B), .CurrentCounter(register_1_out_5), .Instruction(instruction), .NextCounter(out_3));

  // Other names for the same wires on the sheet: Reset = in_1

  // Notes on the sheet:
  //   contents of rom_1 (hex, n*v repeats v):
  //   9883 9082 2990 10990 80028 c2304 1aa82 20120 2b287 4ea20 70c01 d1005 f2005 d1005
endmodule

module extend7to20Aritmethical (
  input  [6:0] in_1,
  output [19:0] out_2
);


  assign out_2 = {{14{in_1[6]}}, in_1[5:0]};
endmodule

module Extend8to12Logical (
  input  [7:0] in_1,
  output [11:0] out_2
);


  assign out_2 = {4'b0000, in_1};
endmodule

module Compare_JUMP (
  input  [19:0] A,
  input  [19:0] B,
  input  [19:0] CurrentCounter,
  input  [19:0] Instruction,
  output [19:0] NextCounter
);

  wire or_1_out, or_2_out;
  wire [19:0] and_1_out, and_2_out, extend8to20logicall_1_out_2, extend13to20logical_1_out_2,
       multiplexer_1_out, multiplexer_2_out;
  wire [19:19] compare_1_out_4, nand_1_out;

  nand nand_1 (nand_1_out[19], Instruction[16], Instruction[18]);
  or or_1 (or_1_out, Instruction[18], Instruction[17], Instruction[16]);
  Compare compare_1 (.A(A), .B(B), .LEG(Instruction[18:16]), .out_4(compare_1_out_4[19]));
  extend8to20Logicall extend8to20logicall_1 (.in_1(Instruction[7:0]), .out_2(extend8to20logicall_1_out_2));
  Extend13to20Logical extend13to20logical_1 (.in_1(Instruction[15:3]), .out_2(extend13to20logical_1_out_2));
  assign and_1_out = {20{compare_1_out_4[19]}} & extend8to20logicall_1_out_2;  // AND_Gate and_1, 20 bits wide
  Multiplexer #(.width(20), .enable("false")) multiplexer_1 (
    .in0(extend13to20logical_1_out_2), .in1(and_1_out), .out(multiplexer_1_out), .sel(or_1_out));
  assign and_2_out = multiplexer_1_out & {20{Instruction[19]}} & {20{nand_1_out[19]}};  // AND_Gate and_2, 20 bits wide
  or or_2 (or_2_out, and_2_out[0], and_2_out[1], and_2_out[2], and_2_out[3], and_2_out[4], and_2_out[5], and_2_out[6], and_2_out[7], and_2_out[8], and_2_out[9], and_2_out[11], and_2_out[12], and_2_out[13], and_2_out[14], and_2_out[15], and_2_out[16], and_2_out[17], and_2_out[18], and_2_out[19], and_2_out[10]);
  Multiplexer #(.width(20), .enable("false")) multiplexer_2 (
    .in0(20'h1), .in1(and_2_out), .out(multiplexer_2_out), .sel(or_2_out));
  Adder adder_1 (.A(CurrentCounter), .B(multiplexer_2_out), .Output(NextCounter));
endmodule

module Extend13to20Logical (
  input  [12:0] in_1,
  output [19:0] out_2
);


  assign out_2 = {{7{1'b0}}, in_1};
endmodule

module extend8to20Logicall (
  input  [7:0] in_1,
  output [19:0] out_2
);


  assign out_2 = {{12{1'b0}}, in_1};
endmodule

module RegisterFlie (
  input  [19:0] D,
  input  load_EN,
  input  [3:0] \reg ,
  input  start,
  input  [3:0] Read_reg2,
  input  [3:0] Read_reg1,
  input  CLK,
  output [19:0] Read_1,
  output [19:0] Read_2
);

  wire demultiplexer_1_out0, demultiplexer_1_out1, demultiplexer_1_out2, demultiplexer_1_out3,
       demultiplexer_1_out4, demultiplexer_1_out5, demultiplexer_1_out6, demultiplexer_1_out7,
       demultiplexer_1_out8, demultiplexer_1_out9, demultiplexer_1_out10, demultiplexer_1_out11,
       demultiplexer_1_out12, demultiplexer_1_out13, demultiplexer_1_out14, demultiplexer_1_out15;
  wire [19:0] register_1_out_5, register_2_out_5, register_3_out_5, register_4_out_5, register_5_out_5,
       register_6_out_5, register_7_out_5, register_8_out_5, register_9_out_5, register_10_out_5,
       register_11_out_5, register_12_out_5, register_13_out_5, register_14_out_5, register_15_out_5,
       register_16_out_5;

  Demultiplexer #(.select(4), .enable("false")) demultiplexer_1 (
    .out0(demultiplexer_1_out0), .out1(demultiplexer_1_out1), .out2(demultiplexer_1_out2),
    .out3(demultiplexer_1_out3), .out4(demultiplexer_1_out4), .out5(demultiplexer_1_out5),
    .out6(demultiplexer_1_out6), .out7(demultiplexer_1_out7), .out8(demultiplexer_1_out8),
    .out9(demultiplexer_1_out9), .out10(demultiplexer_1_out10), .out11(demultiplexer_1_out11),
    .out12(demultiplexer_1_out12), .out13(demultiplexer_1_out13), .out14(demultiplexer_1_out14),
    .out15(demultiplexer_1_out15), .in(load_EN), .sel(\reg ));
  Register register_1 (.D(D), .CLK(CLK), .Load_EN(demultiplexer_1_out0), .clear(start), .out_5(register_1_out_5));
  Register register_2 (.D(D), .CLK(CLK), .Load_EN(demultiplexer_1_out1), .clear(start), .out_5(register_2_out_5));
  Register register_3 (.D(D), .CLK(CLK), .Load_EN(demultiplexer_1_out2), .clear(start), .out_5(register_3_out_5));
  Register register_4 (.D(D), .CLK(CLK), .Load_EN(demultiplexer_1_out3), .clear(start), .out_5(register_4_out_5));
  Register register_5 (.D(D), .CLK(CLK), .Load_EN(demultiplexer_1_out4), .clear(start), .out_5(register_5_out_5));
  Register register_6 (.D(D), .CLK(CLK), .Load_EN(demultiplexer_1_out5), .clear(start), .out_5(register_6_out_5));
  Register register_7 (.D(D), .CLK(CLK), .Load_EN(demultiplexer_1_out6), .clear(start), .out_5(register_7_out_5));
  Register register_8 (.D(D), .CLK(CLK), .Load_EN(demultiplexer_1_out7), .clear(start), .out_5(register_8_out_5));
  Register register_9 (.D(D), .CLK(CLK), .Load_EN(demultiplexer_1_out8), .clear(start), .out_5(register_9_out_5));
  Register register_10 (.D(D), .CLK(CLK), .Load_EN(demultiplexer_1_out9), .clear(start), .out_5(register_10_out_5));
  Register register_11 (.D(D), .CLK(CLK), .Load_EN(demultiplexer_1_out10), .clear(start), .out_5(register_11_out_5));
  Register register_12 (.D(D), .CLK(CLK), .Load_EN(demultiplexer_1_out11), .clear(start), .out_5(register_12_out_5));
  Register register_13 (.D(D), .CLK(CLK), .Load_EN(demultiplexer_1_out12), .clear(start), .out_5(register_13_out_5));
  Register register_14 (.D(D), .CLK(CLK), .Load_EN(demultiplexer_1_out13), .clear(start), .out_5(register_14_out_5));
  Register register_15 (.D(D), .CLK(CLK), .Load_EN(demultiplexer_1_out14), .clear(start), .out_5(register_15_out_5));
  Register register_16 (.D(D), .CLK(CLK), .Load_EN(demultiplexer_1_out15), .clear(start), .out_5(register_16_out_5));
  Multiplexer #(.select(4), .width(20), .enable("false")) multiplexer_1 (
    .in0(register_1_out_5), .in1(register_2_out_5), .in2(register_3_out_5), .in3(register_4_out_5),
    .in4(register_5_out_5), .in5(register_6_out_5), .in6(register_7_out_5), .in7(register_8_out_5),
    .in8(register_9_out_5), .in9(register_10_out_5), .in10(register_11_out_5), .in11(register_12_out_5),
    .in12(register_13_out_5), .in13(register_14_out_5), .in14(register_15_out_5), .in15(register_16_out_5),
    .out(Read_1), .sel(Read_reg1));
  Multiplexer #(.select(4), .width(20), .enable("false")) multiplexer_2 (
    .in0(register_1_out_5), .in1(register_2_out_5), .in2(register_3_out_5), .in3(register_4_out_5),
    .in4(register_5_out_5), .in5(register_6_out_5), .in6(register_7_out_5), .in7(register_8_out_5),
    .in8(register_9_out_5), .in9(register_10_out_5), .in10(register_11_out_5), .in11(register_12_out_5),
    .in12(register_13_out_5), .in13(register_14_out_5), .in14(register_15_out_5), .in15(register_16_out_5),
    .out(Read_2), .sel(Read_reg2));
endmodule

module Load_Store (
  input  in_1,
  input  [3:0] in_2,
  input  [11:0] in_3,
  input  in_4,
  input  in_5,
  input  in_6,
  input  in_7,
  input  [3:0] in_8,
  input  in_9,
  input  [3:0] in_10,
  output [19:0] out_11,
  output [19:0] out_12
);

  wire clock_1_out;
  wire [19:0] ram_1_data;

  Clock clock_1 (.out(clock_1_out));
  RegisterFlie registerflie_1 (
    .D(ram_1_data), .load_EN(in_1), .\reg (in_2), .CLK(clock_1_out), .start(in_5), .Read_reg1(in_8),
    .Read_reg2(in_10), .Read_1(out_11), .Read_2(out_12));
  RAM #(.addrWidth(12), .dataWidth(20), .bus("separate")) ram_1 (
    .addr(in_3), .din(out_11), .data(ram_1_data), .str(in_4), .sel(in_6), .clk(clock_1_out), .ld(in_7),
    .clr(in_9));
endmodule

module RegisterNum (
  input  [19:0] instruction,
  output [3:0] SourceR2,
  output [3:0] SourceR1,
  output [3:0] DestReg,
  output [19:0] Immediate,
  output IsImmediate
);

  wire and_1_out, and_2_out, and_3_out, and_4_out, not_1_out, not_2_out, not_3_out, not_4_out;
  wire [3:0] demultiplexer_1_out0, demultiplexer_1_out1, multiplexer_2_out, multiplexer_3_out,
       multiplexer_4_out;
  wire [19:0] multiplexer_1_out;

  not not_1 (not_1_out, instruction[17]);
  Demultiplexer #(.width(4), .enable("false")) demultiplexer_1 (
    .out0(demultiplexer_1_out0), .out1(demultiplexer_1_out1), .in(instruction[15:12]), .sel(and_1_out));
  and and_1 (and_1_out, instruction[16], not_1_out, instruction[18], instruction[19]);
  not not_2 (not_2_out, instruction[19]);
  not not_3 (not_3_out, instruction[18]);
  not not_4 (not_4_out, instruction[19]);
  Multiplexer #(.width(20), .enable("false")) multiplexer_1 (
    .in0({{13{1'b0}}, instruction[6:0]}), .in1({{11{1'b0}}, instruction[8:0]}), .out(multiplexer_1_out),
    .sel(instruction[18]));
  and and_2 (and_2_out, instruction[16], instruction[18], instruction[19]);
  and and_3 (and_3_out, instruction[17], instruction[18], not_2_out);
  and and_4 (and_4_out, instruction[15], not_3_out, not_4_out);
  Multiplexer #(.width(4), .enable("false")) multiplexer_2 (
    .in0(instruction[6:3]), .in1(instruction[8:5]), .out(multiplexer_2_out), .sel(instruction[18]));
  Multiplexer #(.width(4), .enable("false")) multiplexer_3 (
    .in0(instruction[10:7]), .in1(instruction[12:9]), .out(multiplexer_3_out), .sel(instruction[18]));
  Multiplexer #(.width(4), .enable("false")) multiplexer_4 (
    .in0(instruction[14:11]), .in1(instruction[16:13]), .out(multiplexer_4_out), .sel(instruction[18]));
  Multiplexer #(.width(20), .enable("false")) multiplexer_5 (
    .in0(multiplexer_1_out), .in1({{8{1'b0}}, instruction[11:0]}), .out(Immediate), .sel(instruction[19]));
  or or_1 (IsImmediate, and_2_out, and_3_out, and_4_out);
  Multiplexer #(.width(4), .enable("false")) multiplexer_6 (
    .in0(multiplexer_4_out), .in1(demultiplexer_1_out1), .out(DestReg), .sel(instruction[19]));
  Multiplexer #(.width(4), .enable("false")) multiplexer_7 (
    .in0(multiplexer_2_out), .in1(instruction[11:8]), .out(SourceR2), .sel(instruction[19]));
  Multiplexer #(.width(4), .enable("false")) multiplexer_8 (
    .in0(multiplexer_3_out), .in1(demultiplexer_1_out0), .out(SourceR1), .sel(instruction[19]));
endmodule

module Shrink20to12 (
  input  [19:0] _20Bit,
  output [11:0] _12Bit
);


  assign _12Bit = _20Bit[11:0];
endmodule

module CheckLoadStoreBranch (
  input  [19:0] instruction,
  output LoadEnable,
  output Load,
  output Store
);

  wire not_1_out, not_2_out;

  not not_1 (not_1_out, instruction[17]);
  not not_2 (not_2_out, instruction[19]);
  and and_1 (Load, instruction[16], not_1_out, instruction[18], instruction[19]);
  and and_2 (Store, instruction[16], instruction[17], instruction[18], instruction[19]);
  or or_1 (LoadEnable, not_2_out, Load);
endmodule
